# Fritzing sketch galagino (saved by Fritzing 0.9.6b)
breadboards: 1

parts:
  MH-ET_LIVE_ESP32_DEVKIT1 = MH-ET LIVE ESP32 DEVKIT 38 pins
  TFT1 = Color 320x240 TFT Display, ILI9341 Controller Chip
  R1 = Resistor [tolerance=±5% power=0.25 resistance=270 package=THT]
  Part1 = Mono 2.5W Class D Audio Amplifier - PAM8302
  SP1 = SPEAKER [package=pcb_mount_speaker]
  S1 = Pushbutton [package="[THT]"]
  S2 = Pushbutton [package="[THT]"]
  S3 = Pushbutton [package="[THT]"]
  S4 = Pushbutton [package="[THT]"]
  S5 = Pushbutton [package="[THT]"]

nets:
  VCC: MH-ET_LIVE_ESP32_DEVKIT1.3V3, TFT1.VCC, R1.Pin_1, Part1.VCC
  N1: MH-ET_LIVE_ESP32_DEVKIT1.IO32, TFT1.D/C
  N2: MH-ET_LIVE_ESP32_DEVKIT1.IO33, S3.Pin_1, S3.Pin_2
  N3: MH-ET_LIVE_ESP32_DEVKIT1.IO25, Part1.AIN+
  N4: MH-ET_LIVE_ESP32_DEVKIT1.IO27, TFT1.Reset
  N5: MH-ET_LIVE_ESP32_DEVKIT1.IO14, S4.Pin_1, S4.Pin_2
  N6: MH-ET_LIVE_ESP32_DEVKIT1.IO12, S5.Pin_1, S5.Pin_2
  GND: MH-ET_LIVE_ESP32_DEVKIT1.GND#58, TFT1.GND, Part1.GND, Part1.AIN-, S3.Pin_3, S3.Pin_4, S4.Pin_3, S4.Pin_4, S5.Pin_3, S5.Pin_4
  N7: MH-ET_LIVE_ESP32_DEVKIT1.GND#64, S1.Pin_3, S1.Pin_4, S2.Pin_3, S2.Pin_4
  N8: MH-ET_LIVE_ESP32_DEVKIT1.IO23, TFT1.SDI_(MOSI)
  N9: MH-ET_LIVE_ESP32_DEVKIT1.IO22, S1.Pin_1, S1.Pin_2
  N10: MH-ET_LIVE_ESP32_DEVKIT1.IO21, S2.Pin_1, S2.Pin_2
  N11: MH-ET_LIVE_ESP32_DEVKIT1.IO19, TFT1.SDO_(MISO)
  N12: MH-ET_LIVE_ESP32_DEVKIT1.IO18, TFT1.SCK
  N13: MH-ET_LIVE_ESP32_DEVKIT1.IO5, TFT1.CS
  N14: TFT1.LED, R1.Pin_0
  N15: Part1.VO+, SP1.+
  N16: Part1.VO-, SP1.-

custom parts:
  MH-ET LIVE ESP32 DEVKIT 38 pins: http://mh.nodebb.com/topic/2/mh-et-live-esp32-devkit
  Color 320x240 TFT Display, ILI9341 Controller Chip: 2.2" TFT Display with ILI9341 Controller
  Mono 2.5W Class D Audio Amplifier - PAM8302: A super small but powerful mono amplifier able to deliver up to 2.5 Watts into 4-8 ohm impedance speakers. Inside the miniature chip is a class D controller, able to run from 2.0V-5.5VDC. Since the amp is a class D, its very efficient (over 90% efficient when driving an 8Ω speaker at over half a Watt) - making it perfect for portable and battery-powered projects.
